# Fritzing sketch watering_controller_v1 (saved by Fritzing 0.9.3b)
breadboards: 1

parts:
  WEMOS = WeMos D1 Mini
  R4 = Resistor [tolerance=±5% resistance=330 package=THT]
  V1 = DC Power [voltage=5V]
  P1 = Hirose DF13 Series Header [part_number=PUMP_2 package=DF13C-2P-1.25V]
  D9 = Rectifier Diode [part_number=1N4001 package="300 mil [THT]"]
  TIP120 = TRANSISTOR_NPN [package=sot223]
  U11 = Hirose DF13 Series Header [part_number="SENSOR (moisturel)" package=DF13C-3P-1.25V]
  U12 = Hirose DF13 Series Header [part_number="LED (green / red)" package=DF13C-3P-1.25V]
  R7 = Resistor [tolerance=±5% resistance=470 package=THT]
  R8 = Resistor [tolerance=±5% resistance=470 package=THT]
  R11 = Trimmer Potentiometer [maximum_resistance=10kΩ package=THT]
  R12 = Resistor [tolerance=±5% resistance=10k package=THT]
  RESET = Pushbutton [package="[THT]"]
  U13 = Hirose DF13 Series Header [part_number="SENSOR (SR04)" package=DF13C-4P-1.25V]
  P2 = Hirose DF13 Series Header [part_number=PUMP_1 package=DF13C-2P-1.25V]
  D10 = Rectifier Diode [part_number=1N4001 package="300 mil [THT]"]
  part = attiny85 [package=dip]

nets:
  N1: WEMOS.3V3, U11.2, RESET.Pin_3, RESET.Pin_4, part.Pin_8
  N2: WEMOS.5V, V1.V+, P1.2, D9.cathode, U13.4, P2.2, D10.cathode
  N3: WEMOS.A0, R11.wiper
  N4: WEMOS.D0, R8.Pin_0
  N5: WEMOS.D1, R4.Pin_0
  N6: WEMOS.D2, U13.2
  N7: WEMOS.D3, U13.3
  N8: WEMOS.D5, R7.Pin_0
  N9: WEMOS.D6, part.Pin_2
  N10: WEMOS.D7, RESET.Pin_2
  N11: WEMOS.G, TIP120.E
  N12: WEMOS.RST, part.Pin_3
  N13: R4.Pin_1, TIP120.B
  N14: P1.1, D9.anode, TIP120.C, P2.1, D10.anode
  N15: U11.1, U12.2, R11.leg1, R12.Pin_0, U13.1, part.Pin_4
  N16: U11.3, R11.leg2
  N17: U12.1, R7.Pin_1
  N18: U12.3, R8.Pin_1

// code stored in the sketch: Untitled.ino

